# Fritzing sketch motor_potar (saved by Fritzing 0.4.2b)
breadboards: 1

parts:
  IC1 = H-Bridge [package=THT]
  R1 = Slide Potentiometer  # not connected
  M1 = DC Motor  # not connected
  Arduino1 = Arduino  # not connected

nets:
  GND1: IC1.1_2EN, IC1.1A, IC1.1Y, IC1.GND1, IC1.GND2, IC1.2Y, IC1.2A, IC1.VCC2
  GND3: IC1.3_4EN, IC1.3A, IC1.3Y, IC1.GND3, IC1.GND4, IC1.4Y, IC1.4A, IC1.VCC1
