# Fritzing sketch Relay_XBee (saved by Fritzing 0.4.3b)
breadboards: 1

parts:
  K1 = Relay [package=THT]
  Power_plug1 = Power plug
  R3 = Resistor [resistance=220 package=THT]
  Q2 = NPN-Transistor [package="TO92 [THT]"]
  D2 = Rectifier Diode [package="300 mil [THT]"]
  U1 = XBee
  J1 = Piezo Speaker
  K2 = Relay [package=THT]  # not connected

nets:
  N1: K1.A, J1.pin2
  N2: K1.COIL1, Q2.C, D2.anode
  N3: K1.C1, K1.C2, Power_plug1.VCC
  N4: K1.COIL2, D2.cathode, U1.VCC
  N5: Power_plug1.GND, J1.pin1
  N6: R3.Pin_0, Q2.B
  N7: R3.Pin_1, U1.pin19
  N8: Q2.E, U1.GND
