# Fritzing sketch leds_duinos (saved by Fritzing 0.4.3b)

parts:
  Arduino1 = Arduino
  LED1 = Red LED - 5mm
  LED2 = green LED - 5mm

nets:
  N1: Arduino1.3V3, LED1.cathode, LED2.cathode
  N2: Arduino1.A0, LED1.anode
  N3: Arduino1.A1, LED2.anode
