# Fritzing sketch montage_LM335Z (saved by Fritzing 0.4.3b)
breadboards: 1

parts:
  Arduino1 = Arduino
  R1 = Resistor [resistance=220 package=THT]
  Q1 = PNP-Transistor [package="TO92 [THT]"]

nets:
  N1: Arduino1.+5V, R1.Pin_1
  N2: Arduino1.GND, Q1.C
  N3: Arduino1.A0, R1.Pin_0, Q1.B
