# Fritzing sketch montage_flexsensor (saved by Fritzing 0.4.3b)
breadboards: 1

parts:
  J1 = Basic Force Sensing Resistor (FSR) [package=THT]
  M1 = DC Motor
  R1 = Resistor [resistance=10k package=THT]
  Arduino1 = Arduino

nets:
  N1: J1.pin_0, R1.Pin_1, Arduino1.A0
  N2: J1.pin_1, M1.pin_1, Arduino1.GND
  N3: M1.pin_2, Arduino1.D3
  N4: R1.Pin_0, Arduino1.+5V
